// Logisim project 4-bit Microprocessor.circ as structural Verilog
module HA_1 (
  input  in_1,
  input  in_2,
  output out_3,
  output out_4
);

  and and_1 (out_3, in_1, in_2);
  xor xor_1 (out_4, in_2, in_1);
endmodule

module FA_1 (
  input  in_1,
  input  in_2,
  input  in_3,
  output out_4,
  output out_5
);

  wire and_1_out, and_2_out, xor_1_out;

  and and_1 (and_1_out, in_1, in_2);
  xor xor_1 (xor_1_out, in_1, in_2);
  xor xor_2 (out_4, xor_1_out, in_3);
  and and_2 (and_2_out, xor_1_out, in_3);
  or or_1 (out_5, and_2_out, and_1_out);
endmodule

module FA_4 (
  input  A3,
  input  A2,
  input  A1,
  input  A0,
  input  B3,
  input  B2,
  input  B1,
  input  B0,
  input  Cin,
  output Cout,
  output S3,
  output S2,
  output S1,
  output S0
);

  wire fa_1_2_out_5, fa_1_3_out_5, fa_1_4_out_5;

  FA_1 fa_1_1 (.in_1(A3), .in_2(B3), .in_3(fa_1_2_out_5), .out_4(S3), .out_5(Cout));
  FA_1 fa_1_2 (.in_1(A2), .in_2(B1), .in_3(fa_1_3_out_5), .out_4(S2), .out_5(fa_1_2_out_5));
  FA_1 fa_1_3 (.in_1(A1), .in_2(B1), .in_3(fa_1_4_out_5), .out_4(S1), .out_5(fa_1_3_out_5));
  FA_1 fa_1_4 (.in_1(A0), .in_2(B0), .in_3(Cin), .out_4(S0), .out_5(fa_1_4_out_5));

  assign B2 = B1;
endmodule

module FA_4_BUS (
  input  [3:0] in_1,
  input  [3:0] in_2,
  input  in_3,
  output out_4,
  output [3:0] out_5
);

  wire fa_1_2_out_5, fa_1_3_out_5, fa_1_4_out_5;

  FA_1 fa_1_1 (.in_1(in_1[3]), .in_2(in_2[3]), .in_3(fa_1_2_out_5), .out_4(out_5[3]), .out_5(out_4));
  FA_1 fa_1_2 (.in_1(in_1[2]), .in_2(in_2[2]), .in_3(fa_1_3_out_5), .out_4(out_5[2]), .out_5(fa_1_2_out_5));
  FA_1 fa_1_3 (.in_1(in_1[1]), .in_2(in_2[1]), .in_3(fa_1_4_out_5), .out_4(out_5[1]), .out_5(fa_1_3_out_5));
  FA_1 fa_1_4 (.in_1(in_1[0]), .in_2(in_2[0]), .in_3(in_3), .out_4(out_5[0]), .out_5(fa_1_4_out_5));
endmodule

module INC_2 (
  input  INC,
  input  A0,
  input  A1,
  output Cout,
  output Y0,
  output Y1
);

  wire ha_1_1_out_3;

  HA_1 ha_1_1 (.in_1(INC), .in_2(A0), .out_3(ha_1_1_out_3), .out_4(Y1));
  HA_1 ha_1_2 (.in_1(ha_1_1_out_3), .in_2(A1), .out_3(Cout), .out_4(Y0));
endmodule

module INC_4 (
  input  in_1,
  input  in_2,
  input  in_3,
  input  in_4,
  input  in_5,
  output out_6,
  output out_7,
  output out_8,
  output out_9,
  output out_10
);

  wire ha_1_1_out_3, ha_1_2_out_3, ha_1_3_out_3;

  HA_1 ha_1_1 (.in_1(in_1), .in_2(in_2), .out_3(ha_1_1_out_3), .out_4(out_8));
  HA_1 ha_1_2 (.in_1(ha_1_1_out_3), .in_2(in_3), .out_3(ha_1_2_out_3), .out_4(out_9));
  HA_1 ha_1_3 (.in_1(ha_1_2_out_3), .in_2(in_4), .out_3(ha_1_3_out_3), .out_4(out_10));
  HA_1 ha_1_4 (.in_1(ha_1_3_out_3), .in_2(in_5), .out_3(out_6), .out_4(out_7));
endmodule

module MUX_1 (
  input  A,
  input  B,
  input  S,
  output Y
);

  wire and_1_out, and_2_out, not_1_out;

  not not_1 (not_1_out, S);
  and and_1 (and_1_out, A, S);
  and and_2 (and_2_out, B, not_1_out);
  or or_1 (Y, and_1_out, and_2_out);
endmodule

module MUX_4 (
  input  A3,
  input  A2,
  input  A1,
  input  A0,
  input  B3,
  input  B2,
  input  B1,
  input  B0,
  input  S,
  output Y3,
  output Y2,
  output Y1,
  output Y0
);

  MUX_1 mux_1_1 (.A(A3), .B(B3), .S(S), .Y(Y3));
  MUX_1 mux_1_2 (.A(A2), .B(B2), .S(S), .Y(Y2));
  MUX_1 mux_1_3 (.A(A1), .B(B1), .S(S), .Y(Y1));
  MUX_1 mux_1_4 (.A(A0), .B(B0), .S(S), .Y(Y0));
endmodule

module MUX_4_BUS (
  input  [3:0] B,
  input  [3:0] A,
  input  S,
  output [3:0] Y
);

  MUX_1 mux_1_1 (.A(A[0]), .B(B[0]), .S(S), .Y(Y[0]));
  MUX_1 mux_1_2 (.A(A[1]), .B(B[1]), .S(S), .Y(Y[1]));
  MUX_1 mux_1_3 (.A(A[2]), .B(B[2]), .S(S), .Y(Y[2]));
  MUX_1 mux_1_4 (.A(A[3]), .B(B[3]), .S(S), .Y(Y[3]));
endmodule

module DEMUX_1 (
  input  IN,
  input  S,
  output A,
  output B
);

  wire not_1_out;

  not not_1 (not_1_out, S);
  and and_1 (A, IN, S);
  and and_2 (B, not_1_out, IN);
endmodule

// DEMUX_4_BUS
module DEMUX_4 (
  input  [3:0] in_1,
  input  in_2,
  output [3:0] out_3,
  output [3:0] out_4
);

  DEMUX_1 demux_1_1 (.IN(in_1[0]), .S(in_2), .A(out_3[0]), .B(out_4[0]));
  DEMUX_1 demux_1_2 (.IN(in_1[1]), .S(in_2), .A(out_3[1]), .B(out_4[1]));
  DEMUX_1 demux_1_3 (.IN(in_1[2]), .S(in_2), .A(out_3[2]), .B(out_4[2]));
  DEMUX_1 demux_1_4 (.IN(in_1[3]), .S(in_2), .A(out_3[3]), .B(out_4[3]));
endmodule

module negate (
  input  [3:0] in_1,
  input  in_2,
  output out_3,
  output [3:0] out_4
);

  wire [3:0] xor_1_out;

  assign xor_1_out = in_1 ^ {4{in_2}};  // XOR_Gate xor_1, 4 bits wide
  INC_4 inc_4_1 (
    .in_1(xor_1_out[0]), .in_2(in_2), .in_3(xor_1_out[1]), .in_4(xor_1_out[2]), .in_5(xor_1_out[3]),
    .out_6(out_3), .out_7(out_4[3]), .out_8(out_4[0]), .out_9(out_4[1]), .out_10(out_4[2]));
endmodule

// ADD_SUB_BUS
module ADD_SUBT_BUS (
  input  [3:0] B,
  input  ADD_prime_SUBT,
  input  [3:0] A,
  output out_4,
  output [3:0] S
);

  wire [3:0] inc_4_1_out_8, xor_1_out;

  assign xor_1_out = B ^ {4{ADD_prime_SUBT}};  // XOR_Gate xor_1, 4 bits wide
  INC_4 inc_4_1 (
    .in_1(xor_1_out[0]), .in_2(ADD_prime_SUBT), .in_3(xor_1_out[1]), .in_4(xor_1_out[2]),
    .in_5(xor_1_out[3]), .out_7(inc_4_1_out_8[3]), .out_8(inc_4_1_out_8[0]), .out_9(inc_4_1_out_8[1]),
    .out_10(inc_4_1_out_8[2]));  // open: out_6
  FA_4_BUS fa_4_bus_1 (.in_1(inc_4_1_out_8), .in_2(A), .in_3(1'b0), .out_4(out_4), .out_5(S));
endmodule

module SHIFT (
  input  [3:0] SHNUM,
  input  SHAMT1,
  input  SHAMT0,
  input  L_R_prime,
  output [3:0] SHOUT
);

  wire _1, _2, _3, and_1_out, and_2_out, not_1_out, not_2_out;
  wire [3:0] mux_4_bus_1_y, mux_4_bus_2_y, mux_4_bus_3_y, mux_4_bus_4_y, mux_4_bus_5_y, mux_4_bus_6_y;

  Hex_Digit_Display hex_digit_display_1 (.value(SHNUM));  // open: dp
  Hex_Digit_Display hex_digit_display_2 (.value(SHNUM));  // open: dp
  not not_1 (not_1_out, SHAMT1);
  not not_2 (not_2_out, SHAMT0);
  Hex_Digit_Display hex_digit_display_3 (.value(mux_4_bus_2_y));  // open: dp
  LED led_1 (.in(and_1_out));
  and and_1 (and_1_out, SHAMT0, not_1_out);
  and and_2 (and_2_out, not_2_out, SHAMT1);
  and and_3 (_3, SHAMT1, SHAMT0);
  Hex_Digit_Display hex_digit_display_4 (.value(mux_4_bus_1_y));  // open: dp
  MUX_4_BUS mux_4_bus_1 (.B(SHNUM), .A({SHNUM[2:0], 1'b0}), .S(_1), .Y(mux_4_bus_1_y));
  MUX_4_BUS mux_4_bus_2 (.B(SHNUM), .A({1'b0, SHNUM[3:1]}), .S(_1), .Y(mux_4_bus_2_y));
  LED led_2 (.in(_3));
  LED led_3 (.in(and_2_out));
  or or_1 (_2, _3, and_2_out);
  or or_2 (_1, and_2_out, and_1_out, _3);
  MUX_4_BUS mux_4_bus_3 (.B(mux_4_bus_1_y), .A({mux_4_bus_1_y[2:0], 1'b0}), .S(_2), .Y(mux_4_bus_3_y));
  MUX_4_BUS mux_4_bus_4 (.B(mux_4_bus_2_y), .A({1'b0, mux_4_bus_2_y[3:1]}), .S(_2), .Y(mux_4_bus_4_y));
  Hex_Digit_Display hex_digit_display_5 (.value(mux_4_bus_4_y));  // open: dp
  LED led_4 (.in(_2));
  LED led_5 (.in(_3));
  Hex_Digit_Display hex_digit_display_6 (.value(mux_4_bus_3_y));  // open: dp
  LED led_6 (.in(_1));
  Hex_Digit_Display hex_digit_display_7 (.value(mux_4_bus_5_y));  // open: dp
  MUX_4_BUS mux_4_bus_5 (.B(mux_4_bus_3_y), .A({mux_4_bus_3_y[2:0], 1'b0}), .S(_3), .Y(mux_4_bus_5_y));
  MUX_4_BUS mux_4_bus_6 (.B(mux_4_bus_4_y), .A({1'b0, mux_4_bus_4_y[3:1]}), .S(_3), .Y(mux_4_bus_6_y));
  Hex_Digit_Display hex_digit_display_8 (.value(mux_4_bus_6_y));  // open: dp
  Hex_Digit_Display hex_digit_display_9 (.value(SHOUT));  // open: dp
  MUX_4_BUS mux_4_bus_7 (.B(mux_4_bus_6_y), .A(mux_4_bus_5_y), .S(L_R_prime), .Y(SHOUT));
endmodule

module MULTIPLY (
  input  [3:0] MD,
  input  [3:0] MR,
  output [3:0] PR_UP,
  output [3:0] PR_LO
);

  wire fa_4_bus_3_out_4, fa_4_bus_5_out_4, fa_4_bus_7_out_4, fa_4_bus_9_out_4;
  wire [1:0] add_subt_bus_1_s, add_subt_bus_1_s_2;
  wire [3:0] add_subt_bus_2_s, fa_4_bus_1_out_5, fa_4_bus_2_out_5, fa_4_bus_3_out_5, fa_4_bus_4_out_5,
       fa_4_bus_5_out_5, fa_4_bus_6_out_5, fa_4_bus_7_out_5, mux_4_bus_1_y, mux_4_bus_2_y, mux_4_bus_3_y,
       mux_4_bus_4_y, mux_4_bus_5_y, mux_4_bus_6_y, mux_4_bus_7_y, xor_2_out, xor_3_out;
  wire [3:3] xor_1_out;

  Hex_Digit_Display hex_digit_display_1 (.value(MD));  // open: dp
  Hex_Digit_Display hex_digit_display_2 (.value(MR));  // open: dp
  xor xor_1 (xor_1_out[3], MD[3], MR[3]);
  Hex_Digit_Display hex_digit_display_3 (.value({add_subt_bus_1_s_2, add_subt_bus_1_s}));  // open: dp
  ADD_SUBT_BUS add_subt_bus_1 (
    .B(MD), .ADD_prime_SUBT(MD[3]), .A(4'b0000), .S({add_subt_bus_1_s_2, add_subt_bus_1_s}));  // open: out_4
  ADD_SUBT_BUS add_subt_bus_2 (.B(MR), .ADD_prime_SUBT(MR[3]), .A(4'b0000), .S(add_subt_bus_2_s));  // open: out_4
  Hex_Digit_Display hex_digit_display_4 (.value(add_subt_bus_2_s));  // open: dp
  FA_4_BUS fa_4_bus_1 (
    .in_1({add_subt_bus_1_s_2, add_subt_bus_1_s}), .in_2(4'b0000), .in_3(1'b0), .out_5(fa_4_bus_1_out_5));  // open: out_4
  MUX_4_BUS mux_4_bus_1 (.B(4'b0000), .A(fa_4_bus_1_out_5), .S(add_subt_bus_2_s[0]), .Y(mux_4_bus_1_y));
  LED led_1 (.in(add_subt_bus_2_s[0]));
  FA_4_BUS fa_4_bus_2 (
    .in_1(4'b0000), .in_2({3'b000, add_subt_bus_1_s_2[1]}), .in_3(fa_4_bus_3_out_4), .out_5(fa_4_bus_2_out_5));  // open: out_4
  FA_4_BUS fa_4_bus_3 (
    .in_1({add_subt_bus_1_s_2[0], add_subt_bus_1_s, 1'b0}), .in_2(mux_4_bus_1_y), .in_3(1'b0),
    .out_4(fa_4_bus_3_out_4), .out_5(fa_4_bus_3_out_5));
  Hex_Digit_Display hex_digit_display_5 (.value(mux_4_bus_1_y));  // open: dp
  MUX_4_BUS mux_4_bus_2 (.B(4'b0000), .A(fa_4_bus_2_out_5), .S(add_subt_bus_2_s[1]), .Y(mux_4_bus_2_y));
  MUX_4_BUS mux_4_bus_3 (.B(mux_4_bus_1_y), .A(fa_4_bus_3_out_5), .S(add_subt_bus_2_s[1]), .Y(mux_4_bus_3_y));
  LED led_2 (.in(add_subt_bus_2_s[1]));
  FA_4_BUS fa_4_bus_4 (
    .in_1(mux_4_bus_2_y), .in_2({2'b00, add_subt_bus_1_s_2}), .in_3(fa_4_bus_5_out_4),
    .out_5(fa_4_bus_4_out_5));  // open: out_4
  FA_4_BUS fa_4_bus_5 (
    .in_1(mux_4_bus_3_y), .in_2({add_subt_bus_1_s, 2'b00}), .in_3(1'b0), .out_4(fa_4_bus_5_out_4),
    .out_5(fa_4_bus_5_out_5));
  Hex_Digit_Display hex_digit_display_6 (.value(mux_4_bus_2_y));  // open: dp
  Hex_Digit_Display hex_digit_display_7 (.value(mux_4_bus_3_y));  // open: dp
  MUX_4_BUS mux_4_bus_4 (.B(mux_4_bus_2_y), .A(fa_4_bus_4_out_5), .S(add_subt_bus_2_s[2]), .Y(mux_4_bus_4_y));
  MUX_4_BUS mux_4_bus_5 (.B(mux_4_bus_3_y), .A(fa_4_bus_5_out_5), .S(add_subt_bus_2_s[2]), .Y(mux_4_bus_5_y));
  LED led_3 (.in(add_subt_bus_2_s[2]));
  FA_4_BUS fa_4_bus_6 (
    .in_1(mux_4_bus_4_y), .in_2({1'b0, add_subt_bus_1_s_2, add_subt_bus_1_s[1]}), .in_3(fa_4_bus_7_out_4),
    .out_5(fa_4_bus_6_out_5));  // open: out_4
  FA_4_BUS fa_4_bus_7 (
    .in_1(mux_4_bus_5_y), .in_2({add_subt_bus_1_s[0], 3'b000}), .in_3(1'b0), .out_4(fa_4_bus_7_out_4),
    .out_5(fa_4_bus_7_out_5));
  Hex_Digit_Display hex_digit_display_8 (.value(mux_4_bus_4_y));  // open: dp
  Hex_Digit_Display hex_digit_display_9 (.value(mux_4_bus_5_y));  // open: dp
  LED led_4 (.in(add_subt_bus_2_s[3]));
  MUX_4_BUS mux_4_bus_6 (.B(mux_4_bus_4_y), .A(fa_4_bus_6_out_5), .S(add_subt_bus_2_s[3]), .Y(mux_4_bus_6_y));
  MUX_4_BUS mux_4_bus_7 (.B(mux_4_bus_5_y), .A(fa_4_bus_7_out_5), .S(add_subt_bus_2_s[3]), .Y(mux_4_bus_7_y));
  Hex_Digit_Display hex_digit_display_10 (.value(mux_4_bus_6_y));  // open: dp
  Hex_Digit_Display hex_digit_display_11 (.value(mux_4_bus_7_y));  // open: dp
  assign xor_2_out = {4{xor_1_out[3]}} ^ mux_4_bus_6_y;  // XOR_Gate xor_2, 4 bits wide
  assign xor_3_out = {4{xor_1_out[3]}} ^ mux_4_bus_7_y;  // XOR_Gate xor_3, 4 bits wide
  Hex_Digit_Display hex_digit_display_12 (.value(PR_UP));  // open: dp
  FA_4_BUS fa_4_bus_8 (.in_1(4'b0000), .in_2(xor_2_out), .in_3(fa_4_bus_9_out_4), .out_5(PR_UP));  // open: out_4
  FA_4_BUS fa_4_bus_9 (.in_1(4'b0000), .in_2(xor_3_out), .in_3(xor_1_out[3]), .out_4(fa_4_bus_9_out_4), .out_5(PR_LO));
  Hex_Digit_Display hex_digit_display_13 (.value(PR_LO));  // open: dp
endmodule

module BUFFER_4 (
  input  A3,
  input  A2,
  input  A1,
  input  A0,
  input  EN1,
  input  EN0,
  output Y3,
  output Y2,
  output Y1,
  output Y0
);

  wire and_1_out;

  and and_1 (and_1_out, EN1, EN0);
  assign Y3 = and_1_out ? A3 : 1'bz;  // Controlled_Buffer controlled_buffer_1
  assign Y2 = and_1_out ? A2 : 1'bz;  // Controlled_Buffer controlled_buffer_2
  assign Y1 = and_1_out ? A1 : 1'bz;  // Controlled_Buffer controlled_buffer_3
  assign Y0 = and_1_out ? A0 : 1'bz;  // Controlled_Buffer controlled_buffer_4
endmodule

module _3x8DECODER (
  input  in_1,
  input  in_2,
  input  in_3,
  input  in_4,
  output out_5,
  output out_6,
  output out_7,
  output out_8,
  output out_9,
  output out_10,
  output out_11,
  output out_12
);

  wire not_1_out, not_2_out, not_3_out, not_4_out, not_5_out, not_6_out, not_7_out, not_8_out, not_9_out,
       not_10_out, not_11_out, not_12_out;

  not not_1 (not_1_out, in_1);
  and and_1 (out_5, in_1, in_2, in_3, in_4);
  and and_2 (out_6, in_1, in_2, not_2_out, in_4);
  not not_2 (not_2_out, in_3);
  not not_3 (not_3_out, in_2);
  and and_3 (out_7, in_1, not_3_out, in_3, in_4);
  not not_4 (not_4_out, in_2);
  and and_4 (out_8, in_1, not_4_out, not_5_out, in_4);
  not not_5 (not_5_out, in_3);
  and and_5 (out_9, not_1_out, in_2, in_3, in_4);
  not not_6 (not_6_out, in_1);
  and and_6 (out_10, not_6_out, in_2, not_7_out, in_4);
  not not_7 (not_7_out, in_3);
  not not_8 (not_8_out, in_1);
  not not_9 (not_9_out, in_2);
  and and_7 (out_11, not_8_out, not_9_out, in_3, in_4);
  not not_10 (not_10_out, in_1);
  not not_11 (not_11_out, in_2);
  and and_8 (out_12, not_10_out, not_11_out, not_12_out, in_4);
  not not_12 (not_12_out, in_3);
endmodule

module REG_1 (
  input  A,
  input  EN,
  input  CLK,
  input  CLR_prime,
  output Y
);

  wire not_1_out;

  D_Flip_Flop d_ff_1 (.clk(CLK), .D(A), .Q(Y), .preset(1'b0), .en(EN), .reset(not_1_out));  // open: Qn
  not not_1 (not_1_out, CLR_prime);
endmodule

module REG_4 (
  input  A3,
  input  A2,
  input  A1,
  input  A0,
  input  EN,
  input  CLK,
  input  CLR_prime,
  output Y3,
  output Y2,
  output Y1,
  output Y0
);

  REG_1 reg_1_1 (.A(A3), .EN(EN), .CLK(CLK), .CLR_prime(CLR_prime), .Y(Y3));
  REG_1 reg_1_2 (.A(A2), .EN(EN), .CLK(CLK), .CLR_prime(CLR_prime), .Y(Y2));
  REG_1 reg_1_3 (.A(A1), .EN(EN), .CLK(CLK), .CLR_prime(CLR_prime), .Y(Y1));
  REG_1 reg_1_4 (.A(A0), .EN(EN), .CLK(CLK), .CLR_prime(CLR_prime), .Y(Y0));
endmodule

// ANDOR
module AND_OR (
  input  S2,
  input  S1,
  input  S0,
  input  A3,
  input  A2,
  input  A1,
  input  A0,
  input  B3,
  input  B2,
  input  B1,
  input  B0,
  output Y3,
  output Y2,
  output Y1,
  output Y0
);

  wire mux_4_1_y0, mux_4_1_y1, mux_4_1_y2, mux_4_1_y3, mux_4_2_y0, mux_4_2_y1, mux_4_2_y2, mux_4_2_y3,
       mux_4_3_y0, mux_4_3_y1, mux_4_3_y2, mux_4_3_y3, mux_4_4_y0, mux_4_4_y1, mux_4_4_y2, mux_4_4_y3,
       mux_4_5_y0, mux_4_5_y1, mux_4_5_y2, mux_4_5_y3;
  wire [3:0] and_1_out, mux_4_bus_1_y, nand_4_out, nor_4_out, not_1_out, not_8_out, or_4_out, xnor_4_out,
       xor_4_out;

  Hex_Digit_Display hex_digit_display_1 (.value({A3, A2, A1, A0}));  // open: dp
  Hex_Digit_Display hex_digit_display_2 (.value({B3, B2, B1, B0}));  // open: dp
  Hex_Digit_Display hex_digit_display_3 (.value({1'b0, S2, S1, S0}));  // open: dp
  not not_1 (not_1_out[3], A3);
  not not_2 (not_1_out[2], A2);
  not not_3 (not_1_out[1], A1);
  not not_4 (not_1_out[0], A0);
  and and_1 (and_1_out[0], A3, B3);
  and and_2 (and_1_out[1], A2, B2);
  and and_3 (and_1_out[2], A1, B1);
  and and_4 (and_1_out[3], A0, B0);
  or or_1 (or_4_out[3], A3, B3);
  or or_2 (or_4_out[2], A2, B2);
  or or_3 (or_4_out[1], A1, B1);
  or or_4 (or_4_out[0], A0, B0);
  nor nor_1 (nor_4_out[3], A3, B3);
  nor nor_2 (nor_4_out[2], A2, B2);
  nor nor_3 (nor_4_out[1], A1, B1);
  nor nor_4 (nor_4_out[0], A0, B0);
  nand nand_1 (nand_4_out[3], A3, B3);
  nand nand_2 (nand_4_out[2], A2, B2);
  nand nand_3 (nand_4_out[1], A1, B1);
  nand nand_4 (nand_4_out[0], A0, B0);
  xor xor_1 (xor_4_out[3], A3, B3);
  xor xor_2 (xor_4_out[2], A2, B2);
  xor xor_3 (xor_4_out[2], A1, B1);
  xor xor_4 (xor_4_out[0], A0, B0);
  xnor xnor_1 (xnor_4_out[3], A3, B3);
  xnor xnor_2 (xnor_4_out[2], A2, B2);
  xnor xnor_3 (xnor_4_out[1], A1, B1);
  xnor xnor_4 (xnor_4_out[0], A0, B0);
  not not_5 (not_8_out[3], B3);
  not not_6 (not_8_out[2], B2);
  not not_7 (not_8_out[1], B1);
  not not_8 (not_8_out[0], B0);
  Hex_Digit_Display hex_digit_display_4 (.value(not_1_out));  // open: dp
  Hex_Digit_Display hex_digit_display_5 (.value({and_1_out[0], and_1_out[1], and_1_out[2], and_1_out[3]}));  // open: dp
  Hex_Digit_Display hex_digit_display_6 (.value(or_4_out));  // open: dp
  Hex_Digit_Display hex_digit_display_7 (.value(nor_4_out));  // open: dp
  Hex_Digit_Display hex_digit_display_8 (.value(nand_4_out));  // open: dp
  Hex_Digit_Display hex_digit_display_9 (.value({xor_4_out[3:2], xor_4_out[2], xor_4_out[0]}));  // open: dp
  Hex_Digit_Display hex_digit_display_10 (.value(xnor_4_out));  // open: dp
  Hex_Digit_Display hex_digit_display_11 (.value(not_8_out));  // open: dp
  MUX_4 mux_4_1 (
    .A3(or_4_out[3]), .A2(or_4_out[2]), .A1(or_4_out[1]), .A0(or_4_out[0]), .B3(nor_4_out[3]),
    .B2(nor_4_out[2]), .B1(nor_4_out[1]), .B0(nor_4_out[0]), .S(S2), .Y3(mux_4_1_y3), .Y2(mux_4_1_y2),
    .Y1(mux_4_1_y1), .Y0(mux_4_1_y0));
  MUX_4 mux_4_2 (
    .A3(nand_4_out[3]), .A2(nand_4_out[2]), .A1(nand_4_out[1]), .A0(nand_4_out[0]), .B3(xor_4_out[3]),
    .B2(xor_4_out[2]), .B1(xor_4_out[2]), .B0(xor_4_out[0]), .S(S2), .Y3(mux_4_2_y3), .Y2(mux_4_2_y2),
    .Y1(mux_4_2_y1), .Y0(mux_4_2_y0));
  MUX_4 mux_4_3 (
    .A3(xnor_4_out[3]), .A2(xnor_4_out[2]), .A1(xnor_4_out[1]), .A0(xnor_4_out[0]), .B3(not_8_out[3]),
    .B2(not_8_out[2]), .B1(not_8_out[1]), .B0(not_8_out[0]), .S(S2), .Y3(mux_4_3_y3), .Y2(mux_4_3_y2),
    .Y1(mux_4_3_y1), .Y0(mux_4_3_y0));
  MUX_4_BUS mux_4_bus_1 (
    .B(and_1_out), .A({not_1_out[0], not_1_out[1], not_1_out[2], not_1_out[3]}), .S(S2), .Y(mux_4_bus_1_y));
  MUX_4 mux_4_4 (
    .A3(mux_4_bus_1_y[0]), .A2(mux_4_bus_1_y[1]), .A1(mux_4_bus_1_y[2]), .A0(mux_4_bus_1_y[3]),
    .B3(mux_4_1_y3), .B2(mux_4_1_y2), .B1(mux_4_1_y1), .B0(mux_4_1_y0), .S(S1), .Y3(mux_4_4_y3),
    .Y2(mux_4_4_y2), .Y1(mux_4_4_y1), .Y0(mux_4_4_y0));
  MUX_4 mux_4_5 (
    .A3(mux_4_2_y3), .A2(mux_4_2_y2), .A1(mux_4_2_y1), .A0(mux_4_2_y0), .B3(mux_4_3_y3), .B2(mux_4_3_y2),
    .B1(mux_4_3_y1), .B0(mux_4_3_y0), .S(S1), .Y3(mux_4_5_y3), .Y2(mux_4_5_y2), .Y1(mux_4_5_y1),
    .Y0(mux_4_5_y0));
  MUX_4 mux_4_6 (
    .A3(mux_4_4_y3), .A2(mux_4_4_y2), .A1(mux_4_4_y1), .A0(mux_4_4_y0), .B3(mux_4_5_y3), .B2(mux_4_5_y2),
    .B1(mux_4_5_y1), .B0(mux_4_5_y0), .S(S0), .Y3(Y3), .Y2(Y2), .Y1(Y1), .Y0(Y0));
  Hex_Digit_Display hex_digit_display_12 (.value({Y3, Y2, Y1, Y0}));  // open: dp

  // Notes on the sheet:
  //   FUNCTION
  //   0 = 0000 = 0 = NOT B
  //   1 = 0001 = 1 = NOR A, B
  //   2 = 0010 = 2 = XOR A, B
  //   3 = 0011 = 3 = AND A, B
  //   4 = 0100 = 4 = XNOR A, B
  //   5 = 0101 = 5 = OR A, B
  //   6 = 0110 = 6 = NAND A, B
  //   7 = 0111 = 7 = NOT A
endmodule

module FFALU (
  input  [3:0] A,
  input  [3:0] B,
  input  [3:0] FCN,
  output [3:0] Y
);

  wire [3:0] add_subt_bus_1_s, and_or_1_y0, multiply_1_pr_lo, multiply_1_pr_up, mux_4_bus_1_y, mux_4_bus_2_y,
       mux_4_bus_3_y, mux_4_bus_4_y, mux_4_bus_5_y, shift_1_shout;

  ADD_SUBT_BUS add_subt_bus_1 (.B(B), .ADD_prime_SUBT(FCN[0]), .A(A), .S(add_subt_bus_1_s));  // open: out_4
  MULTIPLY multiply_1 (.MD(A), .MR(B), .PR_UP(multiply_1_pr_up), .PR_LO(multiply_1_pr_lo));
  SHIFT shift_1 (.SHNUM(A), .SHAMT1(B[1]), .SHAMT0(B[0]), .L_R_prime(FCN[0]), .SHOUT(shift_1_shout));
  AND_OR and_or_1 (
    .S2(FCN[2]), .S1(FCN[1]), .S0(FCN[0]), .A3(A[3]), .A2(A[2]), .A1(A[1]), .A0(A[0]), .B3(B[3]), .B2(B[2]),
    .B1(B[1]), .B0(B[0]), .Y3(and_or_1_y0[3]), .Y2(and_or_1_y0[2]), .Y1(and_or_1_y0[1]), .Y0(and_or_1_y0[0]));
  MUX_4_BUS mux_4_bus_1 (.B(B), .A(A), .S(FCN[0]), .Y(mux_4_bus_1_y));
  MUX_4_BUS mux_4_bus_2 (.B(multiply_1_pr_lo), .A(multiply_1_pr_up), .S(FCN[0]), .Y(mux_4_bus_2_y));
  MUX_4_BUS mux_4_bus_3 (.B(shift_1_shout), .A(add_subt_bus_1_s), .S(FCN[1]), .Y(mux_4_bus_3_y));
  MUX_4_BUS mux_4_bus_4 (.B(mux_4_bus_2_y), .A(mux_4_bus_1_y), .S(FCN[1]), .Y(mux_4_bus_4_y));
  MUX_4_BUS mux_4_bus_5 (.B(mux_4_bus_4_y), .A(mux_4_bus_3_y), .S(FCN[2]), .Y(mux_4_bus_5_y));
  MUX_4_BUS mux_4_bus_6 (.B(and_or_1_y0), .A(mux_4_bus_5_y), .S(FCN[3]), .Y(Y));

  // Notes on the sheet:
  //   FUNCTION
  //   0 = 0000 = 0 = NOT B
  //   1 = 0001 = 1 = NOR A, B
  //   2 = 0010 = 2 = XOR A, B
  //   3 = 0011 = 3 = AND A, B
  //   4 = 0100 = 4 = NAND A, B
  //   5 = 0101 = 5 = OR A, B
  //   6 = 0110 = 6 = NAND A, B
  //   7 = 0111 = 7 = NOT A
  //   8 = 1000 = 8 = MULTIPLY LOW
  //   9 = 1001 = 9 = MULTIPLY HIGH
  //   12 = 1100 = C = SHIFT A RIGHT BY B
  //   13 = 1101 = D = SHIFT A LEFT BY B
  //   14 = 1110  = E = ADD A+B
  //   15 = 1111 = F = SUBTRACT A-B
endmodule

module BoumalhabMPU (
  input  [2:0] in_1,
  input  [3:0] in_2,
  input  [3:0] in_3,
  input  Output_Accumulator__Active_High,
  input  Clear_Accum_and_ALU_Reg__Active_Low,
  input  Input_to_Accum__Active_High,
  input  Input_to_ALU_Reg__Active_High,
  input  [3:0] in_8,
  input  ALU_Input_A_B_prime__A___High__B___Low,
  input  Write,
  input  Clock,
  input  Read,
  input  [3:0] in_13,
  input  [3:0] in_14
);

  wire and_1_out, and_2_out, and_3_out, and_4_out, n3x8decoder_1_out_5, n3x8decoder_1_out_6,
       n3x8decoder_1_out_9, n3x8decoder_1_out_10, n3x8decoder_1_out_11, n3x8decoder_1_out_12;
  wire [3:0] buffer_4_1_y0, demux_4_1_out_3, demux_4_1_out_4, ffalu_1_y, reg_4_1_y0, reg_4_2_y0, reg_4_3_y0,
       reg_4_4_y0, reg_4_5_y0, reg_4_6_y0;

  DEMUX_4 demux_4_1 (
    .in_1(buffer_4_1_y0), .in_2(ALU_Input_A_B_prime__A___High__B___Low), .out_3(demux_4_1_out_3),
    .out_4(demux_4_1_out_4));
  Hex_Digit_Display hex_digit_display_1 (.value(demux_4_1_out_4));  // open: dp
  REG_4 reg_4_1 (
    .A3(demux_4_1_out_4[3]), .A2(demux_4_1_out_4[2]), .A1(demux_4_1_out_4[1]), .A0(demux_4_1_out_4[0]),
    .EN(Input_to_ALU_Reg__Active_High), .CLK(Clock), .CLR_prime(Clear_Accum_and_ALU_Reg__Active_Low),
    .Y3(reg_4_1_y0[3]), .Y2(reg_4_1_y0[2]), .Y1(reg_4_1_y0[1]), .Y0(reg_4_1_y0[0]));
  Hex_Digit_Display hex_digit_display_2 (.value(reg_4_1_y0));  // open: dp
  Hex_Digit_Display hex_digit_display_3 (.value(demux_4_1_out_3));  // open: dp
  Hex_Digit_Display hex_digit_display_4 (.value(in_2));  // open: dp
  FFALU ffalu_1 (.A(demux_4_1_out_3), .B(reg_4_1_y0), .FCN(in_2), .Y(ffalu_1_y));
  Hex_Digit_Display hex_digit_display_5 (.value(ffalu_1_y));  // open: dp
  REG_4 reg_4_2 (
    .A3(ffalu_1_y[3]), .A2(ffalu_1_y[2]), .A1(ffalu_1_y[1]), .A0(ffalu_1_y[0]),
    .EN(Input_to_Accum__Active_High), .CLK(Clock), .CLR_prime(Clear_Accum_and_ALU_Reg__Active_Low),
    .Y3(reg_4_2_y0[3]), .Y2(reg_4_2_y0[2]), .Y1(reg_4_2_y0[1]), .Y0(reg_4_2_y0[0]));
  Hex_Digit_Display hex_digit_display_6 (.value(reg_4_2_y0));  // open: dp
  Hex_Digit_Display hex_digit_display_7 (.value({1'b0, in_1}));  // open: dp
  _3x8DECODER u_3x8decoder_1 (
    .in_1(in_1[2]), .in_2(in_1[1]), .in_3(in_1[0]), .in_4(1'b1), .out_5(n3x8decoder_1_out_5),
    .out_6(n3x8decoder_1_out_6), .out_9(n3x8decoder_1_out_9), .out_10(n3x8decoder_1_out_10),
    .out_11(n3x8decoder_1_out_11), .out_12(n3x8decoder_1_out_12));  // open: out_7, out_8
  BUFFER_4 buffer_4_1 (
    .A3(reg_4_2_y0[3]), .A2(reg_4_2_y0[2]), .A1(reg_4_2_y0[1]), .A0(reg_4_2_y0[0]),
    .EN1(Output_Accumulator__Active_High), .EN0(Output_Accumulator__Active_High), .Y3(buffer_4_1_y0[3]),
    .Y2(buffer_4_1_y0[2]), .Y1(buffer_4_1_y0[1]), .Y0(buffer_4_1_y0[0]));
  LED _6 (.in(n3x8decoder_1_out_6));
  LED _0 (.in(n3x8decoder_1_out_12));
  LED _7 (.in(n3x8decoder_1_out_5));
  LED _3 (.in(n3x8decoder_1_out_9));
  LED _1 (.in(n3x8decoder_1_out_11));
  LED _2 (.in(n3x8decoder_1_out_10));
  Hex_Digit_Display hex_digit_display_8 (.value(buffer_4_1_y0));  // open: dp
  and and_1 (and_1_out, Write, n3x8decoder_1_out_12);
  and and_2 (and_2_out, Write, n3x8decoder_1_out_11);
  and and_3 (and_3_out, Write, n3x8decoder_1_out_6);
  and and_4 (and_4_out, Write, n3x8decoder_1_out_5);
  REG_4 reg_4_3 (
    .A3(buffer_4_1_y0[3]), .A2(buffer_4_1_y0[2]), .A1(buffer_4_1_y0[1]), .A0(buffer_4_1_y0[0]),
    .EN(and_1_out), .CLK(Clock), .CLR_prime(1'b1), .Y3(reg_4_3_y0[3]), .Y2(reg_4_3_y0[2]),
    .Y1(reg_4_3_y0[1]), .Y0(reg_4_3_y0[0]));
  REG_4 reg_4_4 (
    .A3(buffer_4_1_y0[3]), .A2(buffer_4_1_y0[2]), .A1(buffer_4_1_y0[1]), .A0(buffer_4_1_y0[0]),
    .EN(and_2_out), .CLK(Clock), .CLR_prime(1'b1), .Y3(reg_4_4_y0[3]), .Y2(reg_4_4_y0[2]),
    .Y1(reg_4_4_y0[1]), .Y0(reg_4_4_y0[0]));
  REG_4 reg_4_5 (
    .A3(buffer_4_1_y0[3]), .A2(buffer_4_1_y0[2]), .A1(buffer_4_1_y0[1]), .A0(buffer_4_1_y0[0]),
    .EN(and_3_out), .CLK(Clock), .CLR_prime(1'b1), .Y3(reg_4_5_y0[3]), .Y2(reg_4_5_y0[2]),
    .Y1(reg_4_5_y0[1]), .Y0(reg_4_5_y0[0]));
  REG_4 reg_4_6 (
    .A3(buffer_4_1_y0[3]), .A2(buffer_4_1_y0[2]), .A1(buffer_4_1_y0[1]), .A0(buffer_4_1_y0[0]),
    .EN(and_4_out), .CLK(Clock), .CLR_prime(1'b1), .Y3(reg_4_6_y0[3]), .Y2(reg_4_6_y0[2]),
    .Y1(reg_4_6_y0[1]), .Y0(reg_4_6_y0[0]));
  Hex_Digit_Display hex_digit_display_9 (.value(reg_4_3_y0));  // open: dp
  Hex_Digit_Display hex_digit_display_10 (.value(reg_4_4_y0));  // open: dp
  Hex_Digit_Display hex_digit_display_11 (.value(reg_4_5_y0));  // open: dp
  Hex_Digit_Display hex_digit_display_12 (.value(reg_4_6_y0));  // open: dp
  BUFFER_4 buffer_4_2 (
    .A3(reg_4_5_y0[3]), .A2(reg_4_5_y0[2]), .A1(reg_4_5_y0[1]), .A0(reg_4_5_y0[0]), .EN1(Read),
    .EN0(n3x8decoder_1_out_6), .Y3(buffer_4_1_y0[3]), .Y2(buffer_4_1_y0[2]), .Y1(buffer_4_1_y0[1]),
    .Y0(buffer_4_1_y0[0]));
  BUFFER_4 buffer_4_3 (
    .A3(reg_4_6_y0[3]), .A2(reg_4_6_y0[2]), .A1(reg_4_6_y0[1]), .A0(reg_4_6_y0[0]), .EN1(Read),
    .EN0(n3x8decoder_1_out_5), .Y3(buffer_4_1_y0[3]), .Y2(buffer_4_1_y0[2]), .Y1(buffer_4_1_y0[1]),
    .Y0(buffer_4_1_y0[0]));
  Hex_Digit_Display hex_digit_display_13 (.value(in_3));  // open: dp
  Hex_Digit_Display hex_digit_display_14 (.value(in_8));  // open: dp
  Hex_Digit_Display hex_digit_display_15 (.value(in_13));  // open: dp
  Hex_Digit_Display hex_digit_display_16 (.value(in_14));  // open: dp
  BUFFER_4 buffer_4_4 (
    .A3(in_3[3]), .A2(in_3[2]), .A1(in_3[1]), .A0(in_3[0]), .EN1(Read), .EN0(n3x8decoder_1_out_12),
    .Y3(buffer_4_1_y0[3]), .Y2(buffer_4_1_y0[2]), .Y1(buffer_4_1_y0[1]), .Y0(buffer_4_1_y0[0]));
  BUFFER_4 buffer_4_5 (
    .A3(in_8[3]), .A2(in_8[2]), .A1(in_8[1]), .A0(in_8[0]), .EN1(Read), .EN0(n3x8decoder_1_out_11),
    .Y3(buffer_4_1_y0[3]), .Y2(buffer_4_1_y0[2]), .Y1(buffer_4_1_y0[1]), .Y0(buffer_4_1_y0[0]));
  BUFFER_4 buffer_4_6 (
    .A3(in_13[3]), .A2(in_13[2]), .A1(in_13[1]), .A0(in_13[0]), .EN1(Read), .EN0(n3x8decoder_1_out_10),
    .Y3(buffer_4_1_y0[3]), .Y2(buffer_4_1_y0[2]), .Y1(buffer_4_1_y0[1]), .Y0(buffer_4_1_y0[0]));
  BUFFER_4 buffer_4_7 (
    .A3(in_14[3]), .A2(in_14[2]), .A1(in_14[1]), .A0(in_14[0]), .EN1(Read), .EN0(n3x8decoder_1_out_9),
    .Y3(buffer_4_1_y0[3]), .Y2(buffer_4_1_y0[2]), .Y1(buffer_4_1_y0[1]), .Y0(buffer_4_1_y0[0]));

  // Notes on the sheet:
  //   FUNCTION
  //   0 = 0000 = 0 = NOT B
  //   1 = 0001 = 1 = NOR A, B
  //   2 = 0010 = 2 = XOR A, B
  //   3 = 0011 = 3 = AND A, B
  //   4 = 0100 = 4 = NAND A, B
  //   5 = 0101 = 5 = OR A, B
  //   6 = 0110 = 6 = NAND A, B
  //   7 = 0111 = 7 = NOT A
  //   8 = 1000 = 8 = MULTIPLY LOW
  //   9 = 1001 = 9 = MULTIPLY HIGH
  //   14 = 1110  = E = ADD A+B
  //   15 = 1111 = F = SUBTRACT A-B
  //   10 = 1010 = A = DIVIDE A/B REMAINDER
  //   11 = 1011 = B = DIVIDE A/B QUOTIENT
  //   12 = 1100 = C = SHIFT A RIGHT BY B
  //   13 = 1101 = D = SHIFT A LEFT BY B
  //   Accumulator
  //   Device Address
  //   Accumulator Bus Access
  //   Device Addfress Lines
  //   4-Bit Data Bus
  //   WOM 0
  //   WOM 1
  //   RAM 6
  //   RAM 7
  //   OUTPUT
  //   OUTPUT
  //   RAM Bus Access
  //   ROM 0
  //   ROM 1
  //   ROM 2
  //   ROM 3
endmodule
